# Fritzing sketch apl-tracker-pcb-shield (saved by Fritzing 0.9.3b)
circuit board: 3.75cm x 2.5cm

parts:
  S1 = Pushbutton [package="[THT]"]
  SW1 = DIP SWITCH [package=dipswitch-02]
  GY3 = female pin header, 5 pins [form="♀ (female)"]
  MPU6051 = female pin header, 5 pins [form="♀ (female)"]
  MPU6050 = female pin header, 4 pins [form="♀ (female)"]
  MPU6052 = female pin header, 1 pin [form="♀ (female)"]

nets:
  N1: S1.Pin_1, S1.Pin_2, MPU6051.pin3
  N2: S1.Pin_3, S1.Pin_4, SW1.1, SW1.2, MPU6051.pin5, MPU6050.pin2
  N3: SW1.3, MPU6051.pin1
  N4: SW1.4, MPU6051.pin2
  N5: GY3.pin1, MPU6050.pin4
  N6: GY3.pin2, MPU6050.pin3
  N7: GY3.pin5, MPU6050.pin1
  N8: MPU6051.pin4, MPU6052.pin1

notes:
  APL
  Head Tracker
  VCC
  GND
  SDA
  SCL
  INT
  D3
  D4
  D5
  +5V
  A4
  A5
  NC
  © Bogdan Bacila
